// Logisim project Cache_Architecture.circ as structural Verilog: 6 circuits, main circuit New Main
module main (
  input  [6:0] Data,
  input  Store,
  input  Load,
  input  [15:0] Address
);

  wire Cache_Controller_regulator, clock_1_out, not_1_out, Tag_Array_hit_miss;
  wire [1:0] Tag_Array_specific_bits;
  wire [6:0] Block_Array_data, Main_Memory_data_out, multiplexer_2_out;
  wire [9:0] Cache_Controller_send_location_to_block_array, multiplexer_1_out, Tag_Array_tag_output;
  wire [15:0] Cache_Controller_send_location_to_main_memory;

  Clock clock_1 (.out(clock_1_out));
  Tag_Array Tag_Array (
    .Clock(clock_1_out), .Location(Address), .Regulator(Cache_Controller_regulator), .Store(Store),
    .Load(Load), .Hit_Miss(Tag_Array_hit_miss), .Tag_Output(Tag_Array_tag_output),
    .Specific_Bits(Tag_Array_specific_bits));
  Cache_Controller Cache_Controller (
    .Send_Location_To_Main_Memory(Cache_Controller_send_location_to_main_memory),
    .Send_Location_To_Block_Array(Cache_Controller_send_location_to_block_array), .Receive_Address(Address),
    .Receive_Specific_Bits(Tag_Array_specific_bits), .Hit_Miss(Tag_Array_hit_miss), .Clock(clock_1_out),
    .Regulator(Cache_Controller_regulator));
  Multiplexer #(.width(10)) multiplexer_1 (
    .in0(Cache_Controller_send_location_to_block_array), .in1(Tag_Array_tag_output), .out(multiplexer_1_out),
    .sel(Tag_Array_hit_miss));  // open: en
  Block_Array Block_Array (
    .Location(multiplexer_1_out), .Write_Data(Data), .Clock(clock_1_out), .Store(Store), .Load(Load),
    .Data(Block_Array_data));  // open: Enable
  not not_1 (not_1_out, Tag_Array_hit_miss);
  Memory Main_Memory (
    .Location(Cache_Controller_send_location_to_main_memory), .Write_Data(Data), .Store(Store),
    .Enable(not_1_out), .Clock(clock_1_out), .Load(Load), .Data_Out(Main_Memory_data_out));
  Multiplexer #(.width(7)) multiplexer_2 (
    .in0(Block_Array_data), .in1(Main_Memory_data_out), .out(multiplexer_2_out), .sel(not_1_out), .en(Load));
  TTY tty_1 (.data(multiplexer_2_out), .clk(clock_1_out));  // open: we, clr
endmodule

module Tag_Array (
  input  Clock,
  input  [15:0] Location,
  input  Store,
  input  Load,
  input  Regulator,
  output Hit_Miss,
  output [9:0] Tag_Output,
  output [1:0] Specific_Bits
);

  wire and_6_out, and_7_out, and_8_out, and_9_out, comparator_1_eq, comparator_2_eq, comparator_3_eq,
       comparator_4_eq, decoder_1_out0, decoder_1_out1, decoder_1_out2, decoder_1_out3, not_1_out, or_1_out,
       or_2_out, or_3_out, priority_encoder_1_p2, priority_encoder_1_p3, priority_encoder_1_p4,
       priority_encoder_1_p5, priority_encoder_1_p6, Ram_1, Ram_2, Ram_3, Ram_4, Store_1, Store_2, Store_3,
       Store_4;
  wire [8:8] and_2_out, and_3_out, and_4_out, and_5_out;
  wire [9:0] Data_1, Data_2, Data_3, Data_4, Input_1, Input_2, Input_3, Input_4, Tag_1, Tag_2, Tag_3, Tag_4;

  Decoder #(.select(2), .disabled(0)) decoder_1 (
    .out0(decoder_1_out0), .out1(decoder_1_out1), .out2(decoder_1_out2), .out3(decoder_1_out3),
    .sel(Specific_Bits), .en(Regulator));
  Multiplexer #(.width(10)) multiplexer_1 (
    .in0(Data_1), .in1({2'b10, Location[15:8]}), .out(Input_1), .sel(decoder_1_out0));  // open: en
  or or_1 (or_1_out, Store, Load);
  not not_1 (not_1_out, Hit_Miss);
  Multiplexer #(.width(10)) multiplexer_2 (
    .in0(Data_2), .in1({2'b10, Location[15:8]}), .out(Input_2), .sel(decoder_1_out1));  // open: en
  or or_2 (or_2_out, Store, Load);
  // Priority_Encoder #(.select(2)) priority_encoder_1: pin names not known; wires that end beside it: Specific_Bits, priority_encoder_1_p2, priority_encoder_1_p3, priority_encoder_1_p4, priority_encoder_1_p5, priority_encoder_1_p6
  and and_1 (priority_encoder_1_p2, not_1_out, or_3_out);
  RAM #(.addrWidth(5), .dataWidth(10), .bus("separate")) u_ram_1 (
    .addr(Location[7:3]), .din(Input_1), .data(Tag_1), .str(Store_1), .sel(or_1_out), .clk(Clock),
    .ld(or_2_out));  // open: clr
  RAM #(.addrWidth(5), .dataWidth(10), .bus("separate")) u_ram_2 (
    .addr(Location[7:3]), .din(Input_2), .data(Tag_2), .str(Store_2), .sel(or_1_out), .clk(Clock),
    .ld(or_2_out));  // open: clr
  RAM #(.addrWidth(5), .dataWidth(10), .bus("separate")) u_ram_3 (
    .addr(Location[7:3]), .din(Input_3), .data(Tag_3), .str(Store_3), .sel(or_1_out), .clk(Clock),
    .ld(or_2_out));  // open: clr
  RAM #(.addrWidth(5), .dataWidth(10), .bus("separate")) u_ram_4 (
    .addr(Location[7:3]), .din(Input_4), .data(Tag_4), .str(Store_4), .sel(or_1_out), .clk(Clock),
    .ld(or_2_out));  // open: clr
  Multiplexer #(.width(10)) multiplexer_3 (
    .in0(Data_3), .in1({2'b10, Location[15:8]}), .out(Input_3), .sel(decoder_1_out2));  // open: en
  not not_2 (priority_encoder_1_p4, Tag_2[9]);
  not not_3 (priority_encoder_1_p6, Tag_4[9]);
  not not_4 (priority_encoder_1_p3, Tag_1[9]);
  not not_5 (priority_encoder_1_p5, Tag_3[9]);
  or or_3 (or_3_out, priority_encoder_1_p3, priority_encoder_1_p4, priority_encoder_1_p5, priority_encoder_1_p6);
  Multiplexer #(.width(10)) multiplexer_4 (
    .in0(Data_4), .in1({2'b10, Location[15:8]}), .out(Input_4), .sel(decoder_1_out3));  // open: en
  Comparator #(.mode("unsigned")) comparator_1 (
    .a(Tag_1[7:0]), .b(Location[15:8]), .eq(comparator_1_eq));  // open: gt, lt
  and and_2 (and_2_out[8], comparator_1_eq, Tag_1[9]);
  Comparator #(.mode("unsigned")) comparator_2 (
    .a(Tag_2[7:0]), .b(Location[15:8]), .eq(comparator_2_eq));  // open: gt, lt
  and and_3 (and_3_out[8], comparator_2_eq, Tag_2[9]);
  Comparator #(.mode("unsigned")) comparator_3 (
    .a(Tag_3[7:0]), .b(Location[15:8]), .eq(comparator_3_eq));  // open: gt, lt
  and and_4 (and_4_out[8], comparator_3_eq, Tag_3[9]);
  Comparator #(.mode("unsigned")) comparator_4 (
    .a(Tag_4[7:0]), .b(Location[15:8]), .eq(comparator_4_eq));  // open: gt, lt
  and and_5 (and_5_out[8], comparator_4_eq, Tag_4[9]);
  or u_Hit_Miss (Hit_Miss, and_2_out[8], and_3_out[8], and_4_out[8], and_5_out[8]);
  and and_6 (and_6_out, Store, Ram_1);
  or or_4 (Store_1, and_6_out, decoder_1_out0);
  and and_7 (and_7_out, Store, Ram_2);
  or or_5 (Store_2, and_7_out, decoder_1_out1);
  assign Data_1 = {1'b0, and_2_out[8], {8{1'b0}}} | Tag_1;  // OR_Gate or_6, 10 bits wide
  assign Data_2 = {1'b0, and_3_out[8], {8{1'b0}}} | Tag_2;  // OR_Gate or_7, 10 bits wide
  or or_8 (Tag_Output[3], and_3_out[8], and_5_out[8]);
  or or_9 (Tag_Output[4], and_4_out[8], and_5_out[8]);
  assign Data_3 = {1'b0, and_4_out[8], {8{1'b0}}} | Tag_3;  // OR_Gate or_10, 10 bits wide
  assign Data_4 = {1'b0, and_5_out[8], {8{1'b0}}} | Tag_4;  // OR_Gate or_11, 10 bits wide
  and and_8 (and_8_out, Store, Ram_3);
  or or_12 (Store_3, and_8_out, decoder_1_out2);
  and and_9 (and_9_out, Store, Ram_4);
  or or_13 (Store_4, and_9_out, decoder_1_out3);
  Decoder #(.select(2), .disabled(0)) decoder_2 (
    .out0(Ram_1), .out1(Ram_2), .out2(Ram_3), .out3(Ram_4), .sel(Tag_Output[4:3]), .en(Store));

  assign {Tag_Output[9:5], Tag_Output[2:0]} = Location[7:0];

  // Other names for the same wires on the sheet: clk = Clock; DATA[7:0] = Location[15:8]; Tag[7:0] = Location[15:8]
endmodule

module Block_Array (
  input  [9:0] Location,
  input  [6:0] Write_Data,
  input  Enable,
  input  Clock,
  input  Store,
  input  Load,
  output [6:0] Data
);

  RAM #(.addrWidth(10), .dataWidth(7), .bus("separate")) ram_1 (
    .addr(Location), .din(Write_Data), .data(Data), .str(Store), .sel(Enable), .clk(Clock), .ld(Load));  // open: clr
endmodule

module Memory (
  input  [15:0] Location,
  input  [6:0] Write_Data,
  input  Clock,
  input  Store,
  input  Load,
  input  Enable,
  output [6:0] Data_Out
);

  RAM #(.addrWidth(16), .dataWidth(7), .bus("separate")) ram_1 (
    .addr(Location), .din(Write_Data), .data(Data_Out), .str(Store), .sel(Enable), .clk(Clock), .ld(Load));  // open: clr
endmodule

module Cache_Controller (
  input  [1:0] Receive_Specific_Bits,
  input  Clock,
  input  [15:0] Receive_Address,
  input  Hit_Miss,
  output [9:0] Send_Location_To_Block_Array,
  output [15:0] Send_Location_To_Main_Memory,
  output Regulator
);

  wire not_1_out;

  Counter #(.width(3), .max('h7)) counter_1 (
    .count(not_1_out), .Q(Send_Location_To_Block_Array[2:0]), .carry(Regulator), .clk(Clock));  // open: load, D, clr
  not not_1 (not_1_out, Hit_Miss);

  assign Send_Location_To_Block_Array[9:3] = {Receive_Address[11:7], Receive_Specific_Bits};
  assign Send_Location_To_Main_Memory = {Receive_Address[15:3], Send_Location_To_Block_Array[2:0]};
endmodule

module New_Main (
  input  [15:0] Address,
  input  [6:0] Data,
  input  Load,
  input  Store
);

  wire and_1_out, Cache_Controller_regulator, Clock_out, not_1_out, not_2_out, or_1_out, or_2_out,
       Tag_Array_hit_miss;
  wire [1:0] Tag_Array_specific_bits;
  wire [6:0] Block_Array_data, Memory_data_out, multiplexer_2_out;
  wire [9:0] Cache_Controller_send_location_to_block_array, multiplexer_1_out, Tag_Array_tag_output;
  wire [15:0] Cache_Controller_send_location_to_main_memory;

  Clock Clock (.out(Clock_out));
  Tag_Array Tag_Array (
    .Clock(Clock_out), .Location(Address), .Regulator(Cache_Controller_regulator), .Store(Store),
    .Load(Load), .Hit_Miss(Tag_Array_hit_miss), .Tag_Output(Tag_Array_tag_output),
    .Specific_Bits(Tag_Array_specific_bits));
  not not_1 (not_1_out, Tag_Array_hit_miss);
  Multiplexer #(.width(10)) multiplexer_1 (
    .in0(Cache_Controller_send_location_to_block_array), .in1(Tag_Array_tag_output), .out(multiplexer_1_out),
    .sel(Tag_Array_hit_miss));  // open: en
  and and_1 (and_1_out, not_1_out, Load);
  or or_1 (or_1_out, and_1_out, Store);
  Cache_Controller Cache_Controller (
    .Send_Location_To_Main_Memory(Cache_Controller_send_location_to_main_memory),
    .Send_Location_To_Block_Array(Cache_Controller_send_location_to_block_array), .Receive_Address(Address),
    .Receive_Specific_Bits(Tag_Array_specific_bits), .Hit_Miss(Tag_Array_hit_miss), .Clock(Clock_out),
    .Regulator(Cache_Controller_regulator));
  Block_Array Block_Array (
    .Location(multiplexer_1_out), .Write_Data(multiplexer_2_out), .Clock(Clock_out), .Store(or_1_out),
    .Load(Load), .Data(Block_Array_data));  // open: Enable
  not not_2 (not_2_out, Tag_Array_hit_miss);
  Multiplexer #(.width(7)) multiplexer_2 (
    .in0(Memory_data_out), .in1(Data), .out(multiplexer_2_out), .sel(Tag_Array_hit_miss));  // open: en
  Memory Memory (
    .Location(Cache_Controller_send_location_to_main_memory), .Store(1'b0), .Enable(not_2_out),
    .Clock(Clock_out), .Load(or_2_out), .Data_Out(Memory_data_out));  // open: Write_Data
  or or_2 (or_2_out, Load, Store);
  TTY tty_1 (.data(Block_Array_data), .clk(Clock_out));  // open: we, clr
endmodule
